# Fritzing sketch 14.Circuit (saved by Fritzing 0.9.3b)
breadboards: 1

parts:
  Grove1 = Grove OLED 128x96
  S1 = Pushbutton [package="[SMD]"]
  R1 = Resistor [tolerance=±5% resistance=10k package="0603 [SMD]"]
  R2 = Photocell (LDR) [package=THT]
  Part1 = Arduino Nano (Rev3.0)

nets:
  GND: Grove1.GND, S1.Pin_1, S1.Pin_2, R1.Pin_0, Part1.GND
  VCC: Grove1.VCC, R2.pin_1, Part1.5V
  N1: Grove1.SDA, Part1.A4
  N2: Grove1.SCL, Part1.A5
  N3: S1.Pin_3, S1.Pin_4, Part1.D2
  N4: R1.Pin_1, R2.pin_0, Part1.A1
