# Fritzing sketch circuit (saved by Fritzing 0.9.2b)
breadboards: 1

parts:
  Part1 = Arduino Nano (Rev3.0)
  OLED1 = 128x32 I2C Monochrome OLED Display
  R1 = Photocell (LDR) [package=THT]
  R2 = Resistor [tolerance=±5% resistance=10k package=THT]
  S1 = Pushbutton [package="[THT]"]

nets:
  GND: Part1.GND, Part1.D2, OLED1.GND, R2.Pin_0, S1.Pin_3, S1.Pin_4
  5V: Part1.5V, OLED1.VIN, R1.pin_1
  N1: Part1.A5, OLED1.SCL
  N2: Part1.A4, OLED1.SDA
  N3: Part1.A1, R1.pin_0, R2.Pin_1
  N4: S1.Pin_1, S1.Pin_2
