# Fritzing sketch blynk (saved by Fritzing 0.9.2b)
breadboards: 1

parts:
  Raspberry_Pi_1 = Raspberry Pi 3 [part_number=RPI-3-V1.2]  # not connected
  LED1 = smd LED [color="Red (633nm)" package="1206 [SMD]"]
  R1 = Resistor [tolerance=±5% resistance=220 package="0402 [SMD]"]
  U1 = NodeMCU V1.0

nets:
  N1: LED1.cathode, U1.GND
  N2: LED1.anode, R1.Pin_1
  N3: R1.Pin_0, U1.D2

custom parts:
  NodeMCU V1.0: ESP8266 based NodeMCU
