# Fritzing sketch nodemcu (saved by Fritzing 0.9.2b)
breadboards: 1

parts:
  U1 = NodeMCU V1.0
  R1 = Photocell (LDR) [package=THT]
  R3 = Resistor [tolerance=±5% resistance=10k package=THT]

nets:
  N1: U1.3V3, R1.pin_0
  N2: U1.GND, R3.Pin_1
  N3: U1.A0, R1.pin_1, R3.Pin_0

custom parts:
  NodeMCU V1.0: ESP8266 based NodeMCU
