# Fritzing sketch sensors (saved by Fritzing 0.9.2b)
breadboards: 1

parts:
  Raspberry_Pi_1 = Raspberry Pi 3 [part_number=RPI-3-V1.2]
  S1 = Momentary Switch [package=ksa_sealed_tac_switch]
  DHT1 = DHT11 Humitidy and Temperature Sensor

nets:
  GND: Raspberry_Pi_1.GND, S1.3, DHT1.GND
  N1: Raspberry_Pi_1.GIPO27, S1.2
  N2: Raspberry_Pi_1.GIPO22, DHT1.DATA
  5V: Raspberry_Pi_1.5V, DHT1.VDD

custom parts:
  DHT11 Humitidy and Temperature Sensor: DHT11 Humidity and Temperature Sensor
