# Fritzing sketch Workplace Buddy (saved by Fritzing 0.9.2b)
breadboards: 1

parts:
  U1 = NodeMCU V1.0
  DHT1 = DHT11 Humitidy and Temperature Sensor
  PIR1 = PIR sensor
  R1 = Photocell (LDR) [package=THT]
  R2 = Resistor [tolerance=±5% resistance=10k package=THT]
  OLED1 = 128x32 I2C Monochrome OLED Display

nets:
  N1: U1.D0, PIR1.SIG
  N2: U1.D2, DHT1.DATA
  N3: U1.D4, OLED1.SDA
  3V3: U1.3V3, DHT1.VDD, R1.pin_0, OLED1.3.3V
  GND: U1.GND, DHT1.GND, PIR1.GND, R2.Pin_1, OLED1.GND
  N4: U1.D5, OLED1.SCL
  VIN: U1.Vin, PIR1.VDD
  N5: U1.A0, R1.pin_1, R2.Pin_0

custom parts:
  NodeMCU V1.0: ESP8266 based NodeMCU
  DHT11 Humitidy and Temperature Sensor: DHT11 Humidity and Temperature Sensor
