# Fritzing sketch weatherstation (saved by Fritzing 0.9.2b)
breadboards: 1

parts:
  U1 = NodeMCU V1.0
  DHT1 = DHT11 Humitidy and Temperature Sensor
  R1 = Photocell (LDR) [package=THT]
  R2 = Resistor [tolerance=±5% resistance=10k package=THT]
  R3 = Resistor [tolerance=±5% resistance=2.2k package=THT]

nets:
  N1: U1.D2, DHT1.DATA
  GND: U1.GND, DHT1.GND, R3.Pin_1
  VIN: U1.Vin, DHT1.VDD, R1.pin_0
  N2: U1.A0, R2.Pin_1, R3.Pin_0
  N3: R1.pin_1, R2.Pin_0

custom parts:
  NodeMCU V1.0: ESP8266 based NodeMCU
  DHT11 Humitidy and Temperature Sensor: DHT11 Humidity and Temperature Sensor
